# Fritzing sketch Sketch (saved by Fritzing 0.9.3b)

parts:
  MCU1 = Raspberry Pi Zero
  Composant1 = Breakout Board for Electret Microphone
  MCU2 = Raspberry Pi Zero
  Grove1 = Grove Buzz

nets:
  N1: MCU1.pin_1, Composant1.VCC
  N2: MCU1.pin_6, Composant1.GND
  N3: MCU1.pin_15, Composant1.AUD
  N4: MCU2.pin_2, MCU2.pin_4, Grove1.VCC
  N5: MCU2.pin_6, MCU2.pin_34, Grove1.GND
  N6: MCU2.pin_15, Grove1.SIG
