# Fritzing sketch sketch (saved by Fritzing 0.9.3b)

parts:
  MCU1 = Raspberry Pi Zero
  Composant1 = Breakout Board for Electret Microphone
  MCU2 = Raspberry Pi Zero
  J1 = Piezo Speaker

nets:
  N1: MCU1.pin_1, Composant1.VCC
  N2: MCU1.pin_6, Composant1.GND
  N3: MCU1.pin_15, Composant1.AUD
  N4: MCU2.pin_1, J1.pin2
  N5: MCU2.pin_15, J1.pin1
